# Fritzing sketch LedPicture (saved by Fritzing 0.9.0b)

parts:
  JACK1 = 2.1mm Barrel Jack with Terminal Block
  Part1 = Arduino Pro Mini v13
  S1 = Momentary Switch [package=tactile-pth]
  NEOPIXEL1 = Neopixel Strip -- White (60/m)
  NEOPIXEL2 = Neopixel Strip -- White (60/m)
  NEOPIXEL4 = Neopixel Strip -- White (60/m)
  NEOPIXEL3 = Neopixel Strip -- White (60/m)
  NEOPIXEL5 = Neopixel Strip -- White (60/m)
  NEOPIXEL6 = Neopixel Strip -- White (60/m)
  NEOPIXEL7 = Neopixel Strip -- White (60/m)
  NEOPIXEL8 = Neopixel Strip -- White (60/m)
  R4 = Resistor [tolerance=±5% resistance=330 package="0603 [SMD]"]
  R5 = Resistor [tolerance=±5% resistance=15k package="0603 [SMD]"]
  R6 = Resistor [tolerance=±5% resistance=220k package="0603 [SMD]"]
  C2 = Electrolytic Capacitor [capacitance=0.22mF voltage=10V package="100 mil [THT, electrolytic]"]

nets:
  N1: JACK1.POS, Part1.VCC, NEOPIXEL1.DO, R5.Pin_1, C2.+
  GND: JACK1.NEG, Part1.GND, NEOPIXEL1.GND, NEOPIXEL8.GND, R6.Pin_1, C2.-
  N2: Part1.D3_PWM, S1.2
  N3: Part1.D2, R4.Pin_0
  N4: S1.1, R5.Pin_0, R6.Pin_0
  N5: NEOPIXEL1.+5V#1, R4.Pin_1
  N6: NEOPIXEL1.+5V#6, NEOPIXEL2.+5V#1
  N7: NEOPIXEL2.+5V#6, NEOPIXEL4.+5V#1
  N8: NEOPIXEL4.+5V#6, NEOPIXEL3.+5V#1
  N9: NEOPIXEL3.+5V#6, NEOPIXEL5.+5V#1
  N10: NEOPIXEL5.+5V#6, NEOPIXEL6.+5V#1
  N11: NEOPIXEL6.+5V#6, NEOPIXEL7.+5V#1
  N12: NEOPIXEL7.+5V#6, NEOPIXEL8.+5V

notes:
  To 5V Battery
  8 X 10 RGB LEDS (WS2812)

custom parts:
  Neopixel Strip -- White (60/m): Neopixel Strip, White, 60 pixels per meter.
